// Logisim project Program-Memory.circ as structural Verilog: 1 circuit, main circuit main
module main (
  input  in_1,
  output out_2
);

  wire alucontrol_1_p2, alucontrol_1_p4, clock_1_out, main_1_p3, main_2_p2, main_2_p4, main_2_p6, main_2_p9,
       main_2_p10, main_2_p11;
  wire [1:0] main_2_p8, main_3_p6;
  wire [31:0] adder_1_out, main_1_p4, main_1_p5, main_1_p6, main_3_p4, main_3_p9, main_3_p10, main_4_p4,
       multiplexer_1_out, multiplexer_2_out, multiplexer_3_out, multiplexer_4_out, ram_1_data, register_q,
       rom_1_data;

  Multiplexer #(.select(2), .width(32)) multiplexer_1 (
    .in0(adder_1_out), .in1(main_1_p5), .in2(main_1_p6), .out(multiplexer_1_out), .sel(main_2_p8));  // open: in3, en
  Clock clock_1 (.out(clock_1_out));
  Register #(.width(32)) register (.D(multiplexer_1_out), .Q(register_q), .clk(clock_1_out), .clr(in_1));  // open: en
  Adder #(.width(32)) adder_1 (.a(register_q), .b(32'h4), .out(adder_1_out));  // open: cin, cout
  ROM #(.addrWidth(10), .dataWidth(32)) rom_1 (.addr(register_q[11:2]), .data(rom_1_data));  // open: sel
  // Immediate__3__main main_1: pin names not known; wires that end beside it: rom_1_data, register_q, main_1_p3, main_1_p4, main_1_p5, main_1_p6
  // AluControl alucontrol_1: pin names not known; wires that end beside it: register_q[14:12], alucontrol_1_p2, register_q[30], alucontrol_1_p4
  // CONTROLLER_main main_2: pin names not known; wires that end beside it: rom_1_data[6:0], main_2_p2, out_2, main_2_p4, alucontrol_1_p2, main_2_p6, main_1_p3, main_2_p8, main_2_p9, main_2_p10, main_2_p11
  // register_file_main main_3: pin names not known; wires that end beside it: rom_1_data[19:15], rom_1_data[24:20], rom_1_data[11:7], main_3_p4, clock_1_out, main_3_p6, in_1, main_2_p4, main_3_p9, main_3_p10
  Multiplexer #(.select(2), .width(32)) multiplexer_2 (
    .in0(main_3_p9), .in1(adder_1_out), .in2(register_q), .out(multiplexer_2_out), .sel(main_3_p6));  // open: in3, en
  Multiplexer #(.width(32)) multiplexer_3 (
    .in0(main_3_p10), .in1(main_1_p4), .out(multiplexer_3_out), .sel(main_2_p6));  // open: en
  // BALU_main BALU: pin names not known; wires that end beside it: main_3_p9, main_3_p10, register_q[14:12], main_2_p2
  // alu_main main_4: pin names not known; wires that end beside it: multiplexer_2_out, multiplexer_3_out, alucontrol_1_p4, main_4_p4
  RAM #(.addrWidth(10), .dataWidth(32), .bus("separate")) ram_1 (
    .addr(main_4_p4[11:2]), .din(main_3_p10), .data(ram_1_data), .str(main_2_p11), .ld(main_2_p9));  // open: sel, clk, clr
  Multiplexer #(.width(32)) multiplexer_4 (
    .in0(main_4_p4), .in1(ram_1_data), .out(multiplexer_4_out), .sel(main_2_p10));  // open: en
  Multiplexer #(.width(32)) multiplexer_5 (
    .in0(multiplexer_4_out), .in1(adder_1_out), .out(main_3_p4), .sel(out_2));  // open: en

  // Notes on the sheet:
  //   contents of rom_1 (hex, n*v repeats v):
  //   300193 400213 419463 4182b3 40320333
endmodule
